# Fritzing sketch Suhu (saved by Fritzing 1.0.1rc)

parts:
  A1 = nozzle-bolt style thermocouple [package=THT]
  A2 = MAX6675 module [package=THT]
  Part1 = LCD1602-I2C
  U2 = LuaNode32 / ESP32 [part_number=ESP32S-PIN30]
  U3 = LM2596 step down module

nets:
  N1: A1.pin1, A2.pin7
  N2: A1.pin2, A2.pin6
  GND: A2.pin1, Part1.GND, U2.GND, U3.OUT-
  N3: A2.pin2, U2.3V3
  N4: A2.pin3, U2.D18
  N5: A2.pin4, U2.D5
  N6: A2.pin5, U2.D19
  VCC: Part1.VCC, U2.Vin, U3.OUT+
  N7: Part1.SDA, U2.D21
  N8: Part1.SCL, U2.D22

custom parts:
  nozzle-bolt style thermocouple: Generic nozzle-bolt style thermocouple.
  MAX6675 module: MAX6675 Module + K Type Thermocouple Sensor Temperature Degrees.
  LCD1602-I2C: A standard character display, usually with 2x16 characters. Comes in many colors with LCM1602 IIC attached.
  LuaNode32 / ESP32: New Image for LuaNode32 DOIT ESP32 DEVKIT V1. Base parts from LuaNode32 / ESP32 ESP32 based LuaNode32 by G.Noorlander DOIT Esp32 DevKit v1 (30 pins long, 11 pins width) by Werner Rothschopf (modified by vanepp Dec 2018)
  LM2596 step down module: LM2596 DC-DC step down power supply module 3 A.
